# Fritzing sketch EKG-Nextion-Display (saved by Fritzing 0.9.2b)
breadboards: 1

parts:
  IC1 = AD8232 HeartRate Monitor [part_number=SEN-12650 chip_label=IC package="DIP (Dual Inline) [THT]"]
  Componente1 = Arduino Nano (Rev3.0)
  U3 = Nokia 6100 Color LCD [package=nokia6100_lcd]

nets:
  GND: IC1.GND, Componente1.GND, U3.CS
  3.3V: IC1.3.3v, Componente1.3V3
  N1: IC1.OUTPUT, Componente1.A0
  N2: IC1.LO-, Componente1.D6
  N3: IC1.LO+, Componente1.D5
  N4: Componente1.D1/TX, U3.SCK
  N5: Componente1.D0/RX, U3.DIO
  N6: Componente1.5V, U3.VDIGITAL

notes:
  NX4024T032_011R
  NEXTION 3,2"

custom parts:
  AD8232 HeartRate Monitor: A DIP stand-in part for whatever IC you want. With 10 pins on a 600mil dual inline package (DIP) footprint.
